// Logisim project lab_5_ALU_design.circ as structural Verilog: 30 circuits, main circuit main
module main (
  input  A0,
  input  A1,
  input  A2,
  input  A3,
  input  B0,
  input  B1,
  input  B2,
  input  B3,
  input  M,
  input  in_10,
  input  in_11,
  input  Read_and_write,
  input  in_13,
  input  in_14
);

  wire clock_1_out, clock_2_out, clock_3_out, comparator_1_out_9, comparator_1_out_10, comparator_1_out_11,
       controlled_buffer_1_out, controlled_buffer_2_out, controlled_buffer_3_out, controlled_buffer_4_out,
       determine_display_circuit_1_f, logic_unit_1_out_11, logic_unit_1_out_12, logic_unit_1_out_13,
       logic_unit_1_out_14, math_unit_1_f0, math_unit_1_f1, math_unit_1_f2, math_unit_1_f3, register_1_q,
       register_2_q, register_3_q, register_4_q, register_5_q, register_6_q, register_7_q, register_8_q,
       register_9_q, register_10_q, register_11_q, register_12_q, seven_seg_display_one_to_fifteen_1_out_5,
       seven_seg_display_one_to_fifteen_1_out_6, seven_seg_display_one_to_fifteen_1_out_7,
       seven_seg_display_one_to_fifteen_1_out_8, seven_seg_display_one_to_fifteen_1_out_9,
       seven_seg_display_one_to_fifteen_1_out_10, seven_seg_display_one_to_fifteen_1_out_11,
       two_channel_four_bit_mux_1_out_10, two_channel_four_bit_mux_1_out_11,
       two_channel_four_bit_mux_1_out_12, two_channel_four_bit_mux_1_out_13;

  Register #(.width(1)) register_1 (.D(A0), .en(in_14), .Q(register_1_q), .clk(clock_1_out));  // open: clr
  Register #(.width(1)) register_2 (.D(A1), .en(in_14), .Q(register_2_q), .clk(clock_1_out));  // open: clr
  Register #(.width(1)) register_3 (.D(A2), .en(in_14), .Q(register_3_q), .clk(clock_1_out));  // open: clr
  Register #(.width(1)) register_4 (.D(A3), .en(in_14), .Q(register_4_q), .clk(clock_1_out));  // open: clr
  Clock clock_1 (.out(clock_1_out));
  math_unit math_unit_1 (
    .A0(A0), .A1(A1), .A2(A2), .A3(A3), .B0(B0), .B1(B1), .B2(B2), .B3(B3), .F0(math_unit_1_f0),
    .F1(math_unit_1_f1), .F2(math_unit_1_f2), .F3(math_unit_1_f3), .in_9(in_10), .in_10(in_11));
  logic_unit logic_unit_1 (
    .A0(A0), .A1(A1), .A2(A2), .A3(A3), .B0(B0), .B1(B1), .B2(B2), .B3(B3), .out_11(logic_unit_1_out_11),
    .out_12(logic_unit_1_out_12), .out_13(logic_unit_1_out_13), .out_14(logic_unit_1_out_14), .in_9(in_10),
    .in_10(in_11));
  LED led_1 (.in(register_1_q));
  LED led_2 (.in(register_2_q));
  LED led_3 (.in(register_3_q));
  LED led_4 (.in(register_4_q));
  Clock clock_2 (.out(clock_2_out));
  two_channel_four_bit_mux two_channel_four_bit_mux_1 (
    .in_1(math_unit_1_f0), .in_2(math_unit_1_f1), .in_3(math_unit_1_f2), .in_4(math_unit_1_f3),
    .in_5(logic_unit_1_out_11), .in_6(logic_unit_1_out_12), .in_7(logic_unit_1_out_13),
    .in_8(logic_unit_1_out_14), .S(M), .out_10(two_channel_four_bit_mux_1_out_10),
    .out_11(two_channel_four_bit_mux_1_out_11), .out_12(two_channel_four_bit_mux_1_out_12),
    .out_13(two_channel_four_bit_mux_1_out_13));
  Register #(.width(1)) register_5 (.D(B0), .en(in_13), .Q(register_5_q), .clk(clock_2_out));  // open: clr
  Register #(.width(1)) register_6 (.D(B1), .en(in_13), .Q(register_6_q), .clk(clock_2_out));  // open: clr
  Register #(.width(1)) register_7 (.D(B2), .en(in_13), .Q(register_7_q), .clk(clock_2_out));  // open: clr
  Register #(.width(1)) register_8 (.D(B3), .en(in_13), .Q(register_8_q), .clk(clock_2_out));  // open: clr
  LED led_5 (.in(register_5_q));
  LED led_6 (.in(register_6_q));
  LED led_7 (.in(register_7_q));
  LED led_8 (.in(register_8_q));
  assign controlled_buffer_1_out = determine_display_circuit_1_f ? two_channel_four_bit_mux_1_out_10 : 1'bz;  // Controlled_Buffer controlled_buffer_1
  assign controlled_buffer_2_out = determine_display_circuit_1_f ? two_channel_four_bit_mux_1_out_11 : 1'bz;  // Controlled_Buffer controlled_buffer_2
  assign controlled_buffer_3_out = determine_display_circuit_1_f ? two_channel_four_bit_mux_1_out_12 : 1'bz;  // Controlled_Buffer controlled_buffer_3
  assign controlled_buffer_4_out = determine_display_circuit_1_f ? two_channel_four_bit_mux_1_out_13 : 1'bz;  // Controlled_Buffer controlled_buffer_4
  determine_display_circuit determine_display_circuit_1 (
    .M(M), .S1(in_10), .S0(in_11), .F(determine_display_circuit_1_f));
  comparator comparator_1 (
    .A3(A3), .B3(B3), .A2(A2), .B2(B2), .A1(A1), .B1(B1), .A0(A0), .B0(B0), .out_9(comparator_1_out_9),
    .out_10(comparator_1_out_10), .out_11(comparator_1_out_11));
  LED led_9 (.in(comparator_1_out_9));
  LED led_10 (.in(comparator_1_out_10));
  LED led_11 (.in(comparator_1_out_11));
  Clock clock_3 (.out(clock_3_out));
  seven_seg_display_one_to_fifteen seven_seg_display_one_to_fifteen_1 (
    .Z(controlled_buffer_1_out), .Y(controlled_buffer_2_out), .X(controlled_buffer_3_out),
    .W(controlled_buffer_4_out), .out_5(seven_seg_display_one_to_fifteen_1_out_5),
    .out_6(seven_seg_display_one_to_fifteen_1_out_6), .out_7(seven_seg_display_one_to_fifteen_1_out_7),
    .out_8(seven_seg_display_one_to_fifteen_1_out_8), .out_9(seven_seg_display_one_to_fifteen_1_out_9),
    .out_10(seven_seg_display_one_to_fifteen_1_out_10), .out_11(seven_seg_display_one_to_fifteen_1_out_11));
  Register #(.width(1)) register_9 (
    .D(two_channel_four_bit_mux_1_out_10), .en(Read_and_write), .Q(register_9_q), .clk(clock_3_out));  // open: clr
  Register #(.width(1)) register_10 (
    .D(two_channel_four_bit_mux_1_out_11), .en(Read_and_write), .Q(register_10_q), .clk(clock_3_out));  // open: clr
  Register #(.width(1)) register_11 (
    .D(two_channel_four_bit_mux_1_out_12), .en(Read_and_write), .Q(register_11_q), .clk(clock_3_out));  // open: clr
  Register #(.width(1)) register_12 (
    .D(two_channel_four_bit_mux_1_out_13), .en(Read_and_write), .Q(register_12_q), .clk(clock_3_out));  // open: clr
  _7_Segment_Display u_7_segment_display_1 (
    .g(seven_seg_display_one_to_fifteen_1_out_11), .f(seven_seg_display_one_to_fifteen_1_out_10),
    .a(seven_seg_display_one_to_fifteen_1_out_5), .b(seven_seg_display_one_to_fifteen_1_out_6),
    .e(seven_seg_display_one_to_fifteen_1_out_9), .d(seven_seg_display_one_to_fifteen_1_out_8),
    .c(seven_seg_display_one_to_fifteen_1_out_7));  // open: dp
  LED led_12 (.in(register_9_q));
  LED led_13 (.in(register_10_q));
  LED led_14 (.in(register_11_q));
  LED led_15 (.in(register_12_q));

  // Notes on the sheet:
  //   S1
  //   S0
endmodule

module Full_Adder_Implementation (
  input  x,
  input  y,
  input  Cin,
  output S,
  output Cout
);

  wire and_1_out, and_2_out, xor_1_out;

  xor xor_1 (xor_1_out, x, y);
  and and_1 (and_1_out, x, y);
  xor xor_2 (S, xor_1_out, Cin);
  and and_2 (and_2_out, xor_1_out, Cin);
  or or_1 (Cout, and_2_out, and_1_out);
endmodule

module four_bit_parallel_adder (
  input  in_1,
  input  in_2,
  input  in_3,
  input  in_4,
  input  in_5,
  input  in_6,
  input  in_7,
  input  in_8,
  output out_9,
  output out_10,
  output out_11,
  output out_12,
  output out_13
);

  wire full_adder_implementation_1_cout, full_adder_implementation_2_cout, full_adder_implementation_3_cout;

  Full_Adder_Implementation full_adder_implementation_1 (
    .x(1'b0), .y(in_1), .Cin(in_2), .S(out_9), .Cout(full_adder_implementation_1_cout));
  Full_Adder_Implementation full_adder_implementation_2 (
    .x(full_adder_implementation_1_cout), .y(in_3), .Cin(in_4), .S(out_10),
    .Cout(full_adder_implementation_2_cout));
  Full_Adder_Implementation full_adder_implementation_3 (
    .x(full_adder_implementation_2_cout), .y(in_5), .Cin(in_6), .S(out_11),
    .Cout(full_adder_implementation_3_cout));
  Full_Adder_Implementation full_adder_implementation_4 (
    .x(full_adder_implementation_3_cout), .y(in_7), .Cin(in_8), .S(out_12), .Cout(out_13));
endmodule

module two_to_four_decoder (
  input  in_1,
  input  in_2,
  output out_3,
  output out_4,
  output out_5,
  output out_6
);

  wire not_1_out, not_2_out, not_3_out, not_4_out;

  not not_1 (not_1_out, in_1);
  not not_2 (not_2_out, in_2);
  not not_3 (not_3_out, in_1);
  not not_4 (not_4_out, in_2);
  and and_1 (out_3, not_1_out, not_2_out);
  and and_2 (out_4, not_3_out, in_2);
  and and_3 (out_5, in_1, not_4_out);
  and and_4 (out_6, in_1, in_2);
endmodule

module four_channel_one_bit_mux (
  input  in_1,
  input  in_2,
  input  in_3,
  input  in_4,
  input  in_5,
  input  in_6,
  output out_7
);

  wire two_to_four_decoder_1_out_3, two_to_four_decoder_1_out_4, two_to_four_decoder_1_out_5,
       two_to_four_decoder_1_out_6;

  assign out_7 = two_to_four_decoder_1_out_3 ? in_1 : 1'bz;  // Controlled_Buffer controlled_buffer_1
  assign out_7 = two_to_four_decoder_1_out_4 ? in_2 : 1'bz;  // Controlled_Buffer controlled_buffer_2
  two_to_four_decoder two_to_four_decoder_1 (
    .in_1(in_5), .in_2(in_6), .out_3(two_to_four_decoder_1_out_3), .out_4(two_to_four_decoder_1_out_4),
    .out_5(two_to_four_decoder_1_out_5), .out_6(two_to_four_decoder_1_out_6));
  assign out_7 = two_to_four_decoder_1_out_5 ? in_3 : 1'bz;  // Controlled_Buffer controlled_buffer_3
  assign out_7 = two_to_four_decoder_1_out_6 ? in_4 : 1'bz;  // Controlled_Buffer controlled_buffer_4
endmodule

module four_channel_four_bit_mux (
  input  in_1,
  input  in_2,
  input  in_3,
  input  in_4,
  input  in_5,
  input  in_6,
  input  in_7,
  input  in_8,
  input  in_9,
  input  in_10,
  input  in_11,
  input  in_12,
  input  in_13,
  input  in_14,
  input  in_15,
  input  in_16,
  input  in_17,
  input  in_18,
  output out_19,
  output out_20,
  output out_21,
  output out_22
);

  four_channel_one_bit_mux four_channel_one_bit_mux_1 (
    .in_1(in_1), .in_2(in_2), .in_3(in_3), .in_4(in_4), .out_7(out_19), .in_5(in_17), .in_6(in_18));
  four_channel_one_bit_mux four_channel_one_bit_mux_2 (
    .in_1(in_5), .in_2(in_6), .in_3(in_7), .in_4(in_8), .out_7(out_20), .in_5(in_17), .in_6(in_18));
  four_channel_one_bit_mux four_channel_one_bit_mux_3 (
    .in_1(in_9), .in_2(in_10), .in_3(in_11), .in_4(in_12), .out_7(out_21), .in_5(in_17), .in_6(in_18));
  four_channel_one_bit_mux four_channel_one_bit_mux_4 (
    .in_1(in_13), .in_2(in_14), .in_3(in_15), .in_4(in_16), .out_7(out_22), .in_5(in_17), .in_6(in_18));
endmodule

module two_channel_four_bit_mux (
  input  in_1,
  input  in_2,
  input  in_3,
  input  in_4,
  input  in_5,
  input  in_6,
  input  in_7,
  input  in_8,
  input  S,
  output out_10,
  output out_11,
  output out_12,
  output out_13
);

  wire and_1_out, and_2_out, and_3_out, and_4_out, and_5_out, and_6_out, and_7_out, and_8_out, not_1_out,
       not_2_out, not_3_out, not_4_out;

  not not_1 (not_1_out, S);
  not not_2 (not_2_out, S);
  not not_3 (not_3_out, S);
  not not_4 (not_4_out, S);
  and and_1 (and_1_out, in_1, not_1_out);
  and and_2 (and_2_out, in_2, not_2_out);
  and and_3 (and_3_out, in_3, not_3_out);
  and and_4 (and_4_out, in_4, not_4_out);
  and and_5 (and_5_out, in_5, S);
  and and_6 (and_6_out, in_6, S);
  and and_7 (and_7_out, in_7, S);
  and and_8 (and_8_out, in_8, S);
  or or_1 (out_10, and_1_out, and_5_out);
  or or_2 (out_11, and_2_out, and_6_out);
  or or_3 (out_12, and_3_out, and_7_out);
  or or_4 (out_13, and_4_out, and_8_out);
endmodule

module four_bit_parallel_subtractor (
  input  in_1,
  input  in_2,
  input  in_3,
  input  in_4,
  input  in_5,
  input  in_6,
  input  in_7,
  input  in_8,
  output out_9,
  output out_10,
  output out_11,
  output out_12,
  output out_13
);

  wire full_adder_implementation_1_cout, full_adder_implementation_2_cout, full_adder_implementation_3_cout,
       not_1_out, not_2_out, not_3_out, not_4_out;

  not not_1 (not_1_out, in_2);
  not not_2 (not_2_out, in_4);
  not not_3 (not_3_out, in_6);
  not not_4 (not_4_out, in_8);
  Full_Adder_Implementation full_adder_implementation_1 (
    .x(1'b1), .y(in_1), .Cin(not_1_out), .S(out_9), .Cout(full_adder_implementation_1_cout));
  Full_Adder_Implementation full_adder_implementation_2 (
    .x(full_adder_implementation_1_cout), .y(in_3), .Cin(not_2_out), .S(out_10),
    .Cout(full_adder_implementation_2_cout));
  Full_Adder_Implementation full_adder_implementation_3 (
    .x(full_adder_implementation_2_cout), .y(in_5), .Cin(not_3_out), .S(out_11),
    .Cout(full_adder_implementation_3_cout));
  Full_Adder_Implementation full_adder_implementation_4 (
    .x(full_adder_implementation_3_cout), .y(in_7), .Cin(not_4_out), .S(out_12), .Cout(out_13));
endmodule

module four_bit_increment (
  input  in_1,
  input  in_2,
  input  in_3,
  input  in_4,
  output out_5,
  output out_6,
  output out_7,
  output out_8,
  output out_9
);

  four_bit_parallel_adder four_bit_parallel_adder_1 (
    .in_1(in_1), .out_9(out_5), .in_2(1'b1), .in_3(in_2), .out_10(out_6), .in_4(1'b0), .in_5(in_3),
    .out_11(out_7), .in_6(1'b0), .in_7(in_4), .out_12(out_8), .in_8(1'b0), .out_13(out_9));
endmodule

module A_segment_display_one_to_nine (
  input  Z,
  input  Y,
  input  X,
  input  W,
  output A
);

  wire xnor_1_out;

  xnor xnor_1 (xnor_1_out, Z, X);
  or or_1 (A, xnor_1_out, Y, W);
endmodule

module B_segment_display_one_to_nine (
  input  Z,
  input  Y,
  input  X,
  output B
);

  wire not_1_out, xnor_1_out;

  xnor xnor_1 (xnor_1_out, Z, Y);
  not not_1 (not_1_out, X);
  or or_1 (B, xnor_1_out, not_1_out);
endmodule

module C_segment_display_one_to_nine (
  input  Z,
  input  Y,
  input  X,
  output C
);

  wire not_1_out;

  not not_1 (not_1_out, Y);
  or or_1 (C, Z, not_1_out, X);
endmodule

module D_segment_display_one_to_nine (
  input  Z,
  input  Y,
  input  X,
  output D
);

  wire and_1_out, and_2_out, and_3_out, and_4_out, not_1_out, not_2_out, not_3_out, not_4_out, not_5_out;

  not not_1 (not_1_out, X);
  not not_2 (not_2_out, Z);
  not not_3 (not_3_out, X);
  not not_4 (not_4_out, Z);
  not not_5 (not_5_out, Y);
  and and_1 (and_1_out, not_3_out, Y);
  and and_2 (and_2_out, not_1_out, not_2_out);
  and and_3 (and_3_out, Y, not_4_out);
  and and_4 (and_4_out, X, not_5_out, Z);
  or or_1 (D, and_2_out, and_1_out, and_3_out, and_4_out);
endmodule

module E_segment_display_one_to_nine (
  input  Z,
  input  Y,
  input  X,
  output E
);

  wire and_1_out, and_2_out, not_1_out, not_2_out, not_3_out;

  not not_1 (not_1_out, X);
  not not_2 (not_2_out, Z);
  and and_1 (and_1_out, not_1_out, not_2_out);
  and and_2 (and_2_out, Y, not_3_out);
  not not_3 (not_3_out, Z);
  or or_1 (E, and_1_out, and_2_out);
endmodule

module F_segment_display_one_to_nine (
  input  Z,
  input  Y,
  input  X,
  input  W,
  output F
);

  wire and_1_out, and_2_out, and_3_out, not_1_out, not_2_out, not_3_out, not_4_out;

  not not_1 (not_1_out, Y);
  not not_2 (not_2_out, Z);
  not not_3 (not_3_out, Y);
  not not_4 (not_4_out, Z);
  and and_1 (and_1_out, X, not_1_out);
  and and_2 (and_2_out, X, not_2_out);
  and and_3 (and_3_out, not_3_out, not_4_out);
  or or_1 (F, and_1_out, and_2_out, and_3_out, W);
endmodule

module G_segment_display_one_to_nine (
  input  Z,
  input  Y,
  input  X,
  input  W,
  output G
);

  wire and_1_out, not_1_out, xor_1_out;

  not not_1 (not_1_out, Z);
  and and_1 (and_1_out, X, not_1_out);
  xor xor_1 (xor_1_out, Y, X);
  or or_1 (G, and_1_out, xor_1_out, W);
endmodule

module seven_segment_display_one_to_nine (
  input  Z,
  input  Y,
  input  X,
  input  W,
  output A,
  output B,
  output C,
  output D,
  output E,
  output F,
  output G
);

  A_segment_display_one_to_nine a_segment_display_one_to_nine_1 (.Z(Z), .Y(Y), .X(X), .W(W), .A(A));
  B_segment_display_one_to_nine b_segment_display_one_to_nine_1 (.Z(Z), .Y(Y), .X(X), .B(B));
  C_segment_display_one_to_nine c_segment_display_one_to_nine_1 (.Z(Z), .Y(Y), .X(X), .C(C));
  D_segment_display_one_to_nine d_segment_display_one_to_nine_1 (.Z(Z), .Y(Y), .X(X), .D(D));
  E_segment_display_one_to_nine e_segment_display_one_to_nine_1 (.Z(Z), .Y(Y), .X(X), .E(E));
  F_segment_display_one_to_nine f_segment_display_one_to_nine_1 (.Z(Z), .Y(Y), .X(X), .W(W), .F(F));
  G_segment_display_one_to_nine g_segment_display_one_to_nine_1 (.Z(Z), .Y(Y), .X(X), .W(W), .G(G));
endmodule

module seven_segment_display_ten_to_fifteen (
  input  Z,
  input  Y,
  input  X,
  output A,
  output B,
  output C,
  output D,
  output E,
  output F,
  output G
);

  wire and_1_out, and_2_out, and_3_out, and_4_out, not_1_out, not_2_out, not_3_out, not_4_out, not_5_out,
       not_6_out, not_7_out, not_8_out, xor_1_out;

  not not_1 (not_1_out, X);
  not not_2 (not_2_out, Z);
  not not_3 (not_3_out, Y);
  not not_4 (not_4_out, Y);
  and and_1 (and_1_out, Y, X);
  and and_2 (and_2_out, not_1_out, not_2_out);
  and and_3 (and_3_out, not_3_out, Z);
  and and_4 (and_4_out, not_4_out, Z);
  xor xor_1 (xor_1_out, Z, X);
  not not_5 (not_5_out, Y);
  not not_6 (not_6_out, Z);
  not not_7 (not_7_out, X);
  not not_8 (not_8_out, Z);
  or or_1 (A, not_6_out, and_1_out);
  or or_2 (B, and_2_out, and_3_out);
  or or_3 (C, and_4_out, not_7_out);
  or or_4 (D, xor_1_out, not_5_out);
  or or_5 (F, Y, not_8_out);
  or or_6 (G, Y, Z);

  assign E = 1'b1;
endmodule

module selector_which_seven_segment (
  input  Y,
  input  X,
  input  W,
  output Select
);

  wire and_1_out, and_2_out;

  and and_1 (and_1_out, X, W);
  and and_2 (and_2_out, Y, W);
  or or_1 (Select, and_1_out, and_2_out);
endmodule

module two_channel_seven_bit_mux (
  input  in_1,
  input  in_2,
  input  in_3,
  input  in_4,
  input  in_5,
  input  in_6,
  input  in_7,
  input  in_8,
  input  in_9,
  input  in_10,
  input  in_11,
  input  in_12,
  input  in_13,
  input  in_14,
  input  S,
  output out_16,
  output out_17,
  output out_18,
  output out_19,
  output out_20,
  output out_21,
  output out_22
);

  wire and_1_out, and_2_out, and_3_out, and_4_out, and_5_out, and_6_out, and_7_out, and_8_out, and_9_out,
       and_10_out, and_11_out, and_12_out, and_13_out, and_14_out, not_1_out, not_2_out, not_3_out,
       not_4_out, not_5_out, not_6_out, not_7_out;

  not not_1 (not_1_out, S);
  not not_2 (not_2_out, S);
  not not_3 (not_3_out, S);
  not not_4 (not_4_out, S);
  not not_5 (not_5_out, S);
  not not_6 (not_6_out, S);
  not not_7 (not_7_out, S);
  and and_1 (and_1_out, in_1, not_1_out);
  and and_2 (and_2_out, in_2, not_2_out);
  and and_3 (and_3_out, in_3, not_3_out);
  and and_4 (and_4_out, in_4, not_4_out);
  and and_5 (and_5_out, in_5, not_5_out);
  and and_6 (and_6_out, in_6, not_6_out);
  and and_7 (and_7_out, in_7, not_7_out);
  and and_8 (and_8_out, in_8, S);
  and and_9 (and_9_out, in_9, S);
  and and_10 (and_10_out, in_10, S);
  and and_11 (and_11_out, in_11, S);
  and and_12 (and_12_out, in_12, S);
  and and_13 (and_13_out, in_13, S);
  and and_14 (and_14_out, in_14, S);
  or or_1 (out_16, and_1_out, and_8_out);
  or or_2 (out_17, and_2_out, and_9_out);
  or or_3 (out_18, and_3_out, and_10_out);
  or or_4 (out_19, and_4_out, and_11_out);
  or or_5 (out_20, and_5_out, and_12_out);
  or or_6 (out_21, and_6_out, and_13_out);
  or or_7 (out_22, and_7_out, and_14_out);
endmodule

module seven_seg_display_one_to_fifteen (
  input  Z,
  input  Y,
  input  X,
  input  W,
  output out_5,
  output out_6,
  output out_7,
  output out_8,
  output out_9,
  output out_10,
  output out_11
);

  wire selector_which_seven_segment_1_select, seven_segment_display_one_to_nine_1_a,
       seven_segment_display_one_to_nine_1_b, seven_segment_display_one_to_nine_1_c,
       seven_segment_display_one_to_nine_1_d, seven_segment_display_one_to_nine_1_e,
       seven_segment_display_one_to_nine_1_f, seven_segment_display_one_to_nine_1_g,
       seven_segment_display_ten_to_fifteen_1_a, seven_segment_display_ten_to_fifteen_1_b,
       seven_segment_display_ten_to_fifteen_1_c, seven_segment_display_ten_to_fifteen_1_d,
       seven_segment_display_ten_to_fifteen_1_e, seven_segment_display_ten_to_fifteen_1_f,
       seven_segment_display_ten_to_fifteen_1_g;

  seven_segment_display_one_to_nine seven_segment_display_one_to_nine_1 (
    .Z(Z), .Y(Y), .X(X), .W(W), .A(seven_segment_display_one_to_nine_1_a),
    .B(seven_segment_display_one_to_nine_1_b), .C(seven_segment_display_one_to_nine_1_c),
    .D(seven_segment_display_one_to_nine_1_d), .E(seven_segment_display_one_to_nine_1_e),
    .F(seven_segment_display_one_to_nine_1_f), .G(seven_segment_display_one_to_nine_1_g));
  seven_segment_display_ten_to_fifteen seven_segment_display_ten_to_fifteen_1 (
    .Z(Z), .Y(Y), .X(X), .A(seven_segment_display_ten_to_fifteen_1_a),
    .B(seven_segment_display_ten_to_fifteen_1_b), .C(seven_segment_display_ten_to_fifteen_1_c),
    .D(seven_segment_display_ten_to_fifteen_1_d), .E(seven_segment_display_ten_to_fifteen_1_e),
    .F(seven_segment_display_ten_to_fifteen_1_f), .G(seven_segment_display_ten_to_fifteen_1_g));
  selector_which_seven_segment selector_which_seven_segment_1 (
    .Y(Y), .X(X), .W(W), .Select(selector_which_seven_segment_1_select));
  two_channel_seven_bit_mux two_channel_seven_bit_mux_1 (
    .in_1(seven_segment_display_one_to_nine_1_a), .in_2(seven_segment_display_one_to_nine_1_b),
    .in_3(seven_segment_display_one_to_nine_1_c), .in_4(seven_segment_display_one_to_nine_1_d),
    .in_5(seven_segment_display_one_to_nine_1_e), .in_6(seven_segment_display_one_to_nine_1_f),
    .in_7(seven_segment_display_one_to_nine_1_g), .in_8(seven_segment_display_ten_to_fifteen_1_a),
    .in_9(seven_segment_display_ten_to_fifteen_1_b), .in_10(seven_segment_display_ten_to_fifteen_1_c),
    .in_11(seven_segment_display_ten_to_fifteen_1_d), .in_12(seven_segment_display_ten_to_fifteen_1_e),
    .in_13(seven_segment_display_ten_to_fifteen_1_f), .in_14(seven_segment_display_ten_to_fifteen_1_g),
    .S(selector_which_seven_segment_1_select), .out_16(out_5), .out_17(out_6), .out_18(out_7),
    .out_19(out_8), .out_20(out_9), .out_21(out_10), .out_22(out_11));
endmodule

module four_bit_and_circuit (
  input  A0,
  input  A1,
  input  A2,
  input  A3,
  input  B0,
  input  B1,
  input  B2,
  input  B3,
  output F0,
  output F1,
  output F2,
  output F3
);

  and and_1 (F0, A0, B0);
  and and_2 (F1, A1, B1);
  and and_3 (F2, A2, B2);
  and and_4 (F3, A3, B3);
endmodule

module four_bit_or_circuit (
  input  A0,
  input  A1,
  input  A2,
  input  A3,
  input  B0,
  input  B1,
  input  B2,
  input  B3,
  output F0,
  output F1,
  output F2,
  output F3
);

  or or_1 (F0, A0, B0);
  or or_2 (F1, A1, B1);
  or or_3 (F2, A2, B2);
  or or_4 (F3, A3, B3);
endmodule

module four_bit_xor_circuit (
  input  A0,
  input  A1,
  input  A2,
  input  A3,
  input  B0,
  input  B1,
  input  B2,
  input  B3,
  output F0,
  output F1,
  output F2,
  output F3
);

  xor xor_1 (F0, A0, B0);
  xor xor_2 (F1, A1, B1);
  xor xor_3 (F2, A2, B2);
  xor xor_4 (F3, A3, B3);
endmodule

module one_complement (
  input  in_1,
  input  in_2,
  input  in_3,
  input  in_4,
  output out_5,
  output out_6,
  output out_7,
  output out_8
);

  not not_1 (out_5, in_1);
  not not_2 (out_6, in_2);
  not not_3 (out_7, in_3);
  not not_4 (out_8, in_4);
endmodule

module two_complement (
  input  in_1,
  input  in_2,
  input  in_3,
  input  in_4,
  output out_5,
  output out_6,
  output out_7,
  output out_8,
  output out_9
);

  wire not_1_out, not_2_out, not_3_out, not_4_out;

  not not_1 (not_1_out, in_1);
  not not_2 (not_2_out, in_2);
  not not_3 (not_3_out, in_3);
  not not_4 (not_4_out, in_4);
  four_bit_parallel_adder four_bit_parallel_adder_1 (
    .in_1(1'b1), .out_9(out_5), .in_2(not_1_out), .in_3(1'b0), .out_10(out_6), .in_4(not_2_out), .in_5(1'b0),
    .out_11(out_7), .in_6(not_3_out), .in_7(1'b0), .out_12(out_8), .in_8(not_4_out), .out_13(out_9));
endmodule

module math_unit (
  input  A0,
  input  A1,
  input  A2,
  input  A3,
  input  B0,
  input  B1,
  input  B2,
  input  B3,
  input  in_9,
  input  in_10,
  output F0,
  output F1,
  output F2,
  output F3
);

  wire four_bit_increment_1_out_5, four_bit_increment_1_out_6, four_bit_increment_1_out_7,
       four_bit_increment_1_out_8, four_bit_parallel_adder_1_out_9, four_bit_parallel_adder_1_out_10,
       four_bit_parallel_adder_1_out_11, four_bit_parallel_adder_1_out_12,
       four_bit_parallel_subtractor_1_out_9, four_bit_parallel_subtractor_1_out_10,
       four_bit_parallel_subtractor_1_out_11, four_bit_parallel_subtractor_1_out_12, two_complement_1_out_5,
       two_complement_1_out_6, two_complement_1_out_7, two_complement_1_out_8;

  four_bit_parallel_adder four_bit_parallel_adder_1 (
    .in_1(A0), .out_9(four_bit_parallel_adder_1_out_9), .in_2(B0), .in_3(A1),
    .out_10(four_bit_parallel_adder_1_out_10), .in_4(B1), .in_5(A2),
    .out_11(four_bit_parallel_adder_1_out_11), .in_6(B2), .in_7(A3),
    .out_12(four_bit_parallel_adder_1_out_12), .in_8(B3));  // open: out_13
  four_bit_parallel_subtractor four_bit_parallel_subtractor_1 (
    .in_1(A0), .in_2(B0), .in_3(A1), .in_4(B1), .in_5(A2), .in_6(B2), .in_7(A3), .in_8(B3),
    .out_9(four_bit_parallel_subtractor_1_out_9), .out_10(four_bit_parallel_subtractor_1_out_10),
    .out_11(four_bit_parallel_subtractor_1_out_11), .out_12(four_bit_parallel_subtractor_1_out_12));  // open: out_13
  two_complement two_complement_1 (
    .in_1(B0), .in_2(B1), .in_3(B2), .in_4(B3), .out_5(two_complement_1_out_5),
    .out_6(two_complement_1_out_6), .out_7(two_complement_1_out_7), .out_8(two_complement_1_out_8));  // open: out_9
  four_bit_increment four_bit_increment_1 (
    .in_1(A0), .in_2(A1), .in_3(A2), .in_4(A3), .out_5(four_bit_increment_1_out_5),
    .out_6(four_bit_increment_1_out_6), .out_7(four_bit_increment_1_out_7), .out_8(four_bit_increment_1_out_8));  // open: out_9
  four_channel_four_bit_mux four_channel_four_bit_mux_1 (
    .in_1(four_bit_parallel_adder_1_out_9), .in_2(four_bit_parallel_subtractor_1_out_9),
    .in_3(two_complement_1_out_5), .in_4(four_bit_increment_1_out_5),
    .in_5(four_bit_parallel_adder_1_out_10), .in_6(four_bit_parallel_subtractor_1_out_10),
    .in_7(two_complement_1_out_6), .in_8(four_bit_increment_1_out_6),
    .in_9(four_bit_parallel_adder_1_out_11), .in_10(four_bit_parallel_subtractor_1_out_11),
    .in_11(two_complement_1_out_7), .in_12(four_bit_increment_1_out_7),
    .in_13(four_bit_parallel_adder_1_out_12), .in_14(four_bit_parallel_subtractor_1_out_12),
    .in_15(two_complement_1_out_8), .in_16(four_bit_increment_1_out_8), .out_19(F0), .out_20(F1),
    .out_21(F2), .out_22(F3), .in_17(in_9), .in_18(in_10));

  // Notes on the sheet:
  //   S0
  //   S1
endmodule

module logic_unit (
  input  A0,
  input  A1,
  input  A2,
  input  A3,
  input  B0,
  input  B1,
  input  B2,
  input  B3,
  input  in_9,
  input  in_10,
  output out_11,
  output out_12,
  output out_13,
  output out_14
);

  wire four_bit_and_circuit_1_f0, four_bit_and_circuit_1_f1, four_bit_and_circuit_1_f2,
       four_bit_and_circuit_1_f3, four_bit_or_circuit_1_f0, four_bit_or_circuit_1_f1,
       four_bit_or_circuit_1_f2, four_bit_or_circuit_1_f3, four_bit_xor_circuit_1_f0,
       four_bit_xor_circuit_1_f1, four_bit_xor_circuit_1_f2, four_bit_xor_circuit_1_f3,
       one_complement_1_out_5, one_complement_1_out_6, one_complement_1_out_7, one_complement_1_out_8;

  four_bit_and_circuit four_bit_and_circuit_1 (
    .A0(A0), .A1(A1), .A2(A2), .A3(A3), .B0(B0), .B1(B1), .B2(B2), .B3(B3), .F0(four_bit_and_circuit_1_f0),
    .F1(four_bit_and_circuit_1_f1), .F2(four_bit_and_circuit_1_f2), .F3(four_bit_and_circuit_1_f3));
  four_bit_or_circuit four_bit_or_circuit_1 (
    .A0(A0), .A1(A1), .A2(A2), .A3(A3), .B0(B0), .B1(B1), .B2(B2), .B3(B3), .F0(four_bit_or_circuit_1_f0),
    .F1(four_bit_or_circuit_1_f1), .F2(four_bit_or_circuit_1_f2), .F3(four_bit_or_circuit_1_f3));
  four_bit_xor_circuit four_bit_xor_circuit_1 (
    .A0(A0), .A1(A1), .A2(A2), .A3(A3), .B0(B0), .B1(B1), .B2(B2), .B3(B3), .F0(four_bit_xor_circuit_1_f0),
    .F1(four_bit_xor_circuit_1_f1), .F2(four_bit_xor_circuit_1_f2), .F3(four_bit_xor_circuit_1_f3));
  one_complement one_complement_1 (
    .in_1(B0), .in_2(B1), .in_3(B2), .in_4(B3), .out_5(one_complement_1_out_5),
    .out_6(one_complement_1_out_6), .out_7(one_complement_1_out_7), .out_8(one_complement_1_out_8));
  four_channel_four_bit_mux four_channel_four_bit_mux_1 (
    .in_1(four_bit_and_circuit_1_f0), .in_2(four_bit_or_circuit_1_f0), .in_3(four_bit_xor_circuit_1_f0),
    .in_4(one_complement_1_out_5), .in_5(four_bit_and_circuit_1_f1), .in_6(four_bit_or_circuit_1_f1),
    .in_7(four_bit_xor_circuit_1_f1), .in_8(one_complement_1_out_6), .in_9(four_bit_and_circuit_1_f2),
    .in_10(four_bit_or_circuit_1_f2), .in_11(four_bit_xor_circuit_1_f2), .in_12(one_complement_1_out_7),
    .in_13(four_bit_and_circuit_1_f3), .in_14(four_bit_or_circuit_1_f3), .in_15(four_bit_xor_circuit_1_f3),
    .in_16(one_complement_1_out_8), .out_19(out_11), .out_20(out_12), .out_21(out_13), .out_22(out_14),
    .in_17(in_9), .in_18(in_10));
endmodule

module determine_display_circuit (
  input  M,
  input  S1,
  input  S0,
  output F
);

  wire and_1_out, nor_1_out, not_1_out;

  not not_1 (not_1_out, M);
  nor nor_1 (nor_1_out, M, S1);
  and and_1 (and_1_out, not_1_out, S0);
  or or_1 (F, nor_1_out, and_1_out);
endmodule

module comparator (
  input  A3,
  input  B3,
  input  A2,
  input  B2,
  input  A1,
  input  B1,
  input  A0,
  input  B0,
  output out_9,
  output out_10,
  output out_11
);

  wire and_1_out, and_2_out, and_3_out, and_4_out, and_5_out, and_6_out, and_7_out, and_8_out, and_9_out,
       and_10_out, and_11_out, and_12_out, and_13_out, and_14_out, nor_1_out, nor_2_out, nor_3_out,
       nor_4_out, not_1_out, not_2_out, not_3_out, not_4_out, not_5_out, not_6_out, not_7_out, not_8_out;

  not not_1 (not_1_out, A3);
  not not_2 (not_2_out, B3);
  not not_3 (not_3_out, A2);
  not not_4 (not_4_out, B2);
  not not_5 (not_5_out, A1);
  not not_6 (not_6_out, B1);
  not not_7 (not_7_out, A0);
  not not_8 (not_8_out, B0);
  and and_1 (and_1_out, not_1_out, B3);
  and and_2 (and_2_out, A3, not_2_out);
  and and_3 (and_3_out, not_3_out, B2);
  and and_4 (and_4_out, A2, not_4_out);
  and and_5 (and_5_out, not_5_out, B1);
  and and_6 (and_6_out, A1, not_6_out);
  and and_7 (and_7_out, not_7_out, B0);
  and and_8 (and_8_out, A0, not_8_out);
  nor nor_1 (nor_1_out, and_3_out, and_4_out);
  nor nor_2 (nor_2_out, and_5_out, and_6_out);
  nor nor_3 (nor_3_out, and_7_out, and_8_out);
  nor nor_4 (nor_4_out, and_1_out, and_2_out);
  and and_9 (and_9_out, nor_4_out, and_4_out);
  and and_10 (and_10_out, nor_4_out, nor_1_out, and_5_out);
  and and_11 (and_11_out, nor_4_out, nor_1_out, and_6_out);
  and and_12 (and_12_out, nor_4_out, nor_1_out, nor_2_out, and_7_out);
  and and_13 (and_13_out, nor_4_out, and_3_out);
  and and_14 (and_14_out, nor_4_out, nor_1_out, nor_2_out, and_8_out);
  and and_15 (out_11, nor_4_out, nor_1_out, nor_2_out, nor_3_out);
  or or_1 (out_9, and_1_out, and_13_out, and_10_out, and_12_out);
  or or_2 (out_10, and_2_out, and_9_out, and_11_out, and_14_out);
endmodule
